# Fritzing sketch wiring (saved by Fritzing 0.9.2b)
breadboards: 1

parts:
  Q1 = Basic FET N-Channel [package="D2Pak [SMD]"]
  Q2 = Basic FET N-Channel [package="TO220 [THT]"]
  Q3 = Basic FET N-Channel [package="TO220 [THT]"]
  Q4 = Basic FET N-Channel [package="TO220 [THT]"]
  LED1 = RGB LED (com. cathode, rbg) [package="5 mm [THT]"]
  R1 = Resistor [tolerance=±5% resistance=10k package="2010 [SMD]"]
  R2 = Resistor [tolerance=±5% resistance=10k package="2010 [SMD]"]
  R3 = Resistor [tolerance=±5% resistance=10k package="2010 [SMD]"]
  S1 = Round Pushbutton
  LED2 = smd LED [color="White (4500K)" package="0603 [SMD]"]
  S2 = Square Pushbutton
  Raspberry_Pi1 = Raspberry Pi B rev2

nets:
  N1: Q1.Gate, Raspberry_Pi1.GPIO_17
  N2: Q1.drain, LED1.blue_anode
  N3: Q1.source, Q2.source, Q3.source, Q4.source, R1.Pin_1, R2.Pin_1, R3.Pin_1, S1.leg1, S2.leg1, Raspberry_Pi1.GND
  N4: Q2.gate, R2.Pin_0, Raspberry_Pi1.GPIO_27
  N5: Q2.drain, LED1.red_anode
  N6: Q3.gate, R3.Pin_0, Raspberry_Pi1.GPIO_22
  N7: Q3.drain, LED1.green_anode
  N8: Q4.gate, Raspberry_Pi1.GPIO_4
  N9: Q4.drain, LED2.anode
  N10: LED1.common_cathode, LED2.cathode
  N11: S1.leg0, Raspberry_Pi1.GPIO_23
  N12: S2.leg0, Raspberry_Pi1.GPIO_24

notes:
  GND
  VCC 12V
  Exit button
  Trigger (illuminated)
